// Logisim project SelectionSort.circ as structural Verilog: 2 circuits, main circuit main
module main (
  input  done,
  input  [7:0] data,
  input  data_av
);

  wire clk_out, not_1_out, rst_out, undriven_2, undriven_4;
  wire [7:0] ram_1_data, undriven, undriven_3;

  Clock clk (.out(clk_out));
  Button rst (.out(rst_out));
  not not_1 (not_1_out, undriven_4);
  RAM ram_1 (.addr(undriven_3), .data(ram_1_data), .sel(undriven_2), .clk(clk_out), .ld(undriven_4));  // open: clr
  assign ram_1_data = not_1_out ? undriven : 8'bz;  // Controlled_Buffer controlled_buffer_1

  // Notes on the sheet:
  //   data_in
  //   data_out
endmodule

module Selection_Sort (
  input  [7:0] data_in,
  input  wrMin,
  input  selSum0min,
  input  selSum0i,
  input  wrI,
  input  wrStartAddr,
  input  selSum1i,
  input  selInc,
  input  wrSize,
  input  selComp,
  input  wrI_2,
  input  [7:0] data,
  input  wrOrder,
  output lt_size
);

  wire clk, rst;
  wire [6:0] subtractor_1_out;
  wire [7:0] adder_1_out, multiplexer_1_out, multiplexer_2_out, multiplexer_3_out, multiplexer_4_out,
       multiplexer_5_out, reg_i_q, reg_J_q, reg_order_q, reg_size_q, reg_startAddr_q, undriven;

  Clock clock_1 (.out(clk));
  // Probe on data
  Button button_1 (.out(rst));
  Register reg_startAddr (.D(data), .en(wrStartAddr), .Q(reg_startAddr_q), .clk(clk), .clr(rst));
  Register reg_size (.D(data), .en(wrSize), .Q(reg_size_q), .clk(clk), .clr(rst));
  Register reg_order (.D(data), .en(wrOrder), .Q(reg_order_q), .clk(clk), .clr(rst));
  Multiplexer #(.width(8), .disabled(0), .enable("false")) multiplexer_1 (
    .in0(adder_1_out), .in1(undriven), .out(multiplexer_1_out), .sel(selSum0i));
  Multiplexer #(.width(8), .disabled(0), .enable("false")) multiplexer_2 (
    .in0(multiplexer_1_out), .in1(reg_startAddr_q), .out(multiplexer_2_out), .sel(selSum1i));
  Register reg_i (.D(multiplexer_2_out), .en(wrI), .Q(reg_i_q), .clk(clk), .clr(rst));
  Register reg_J (.D(adder_1_out), .en(wrI_2), .Q(reg_J_q), .clk(clk), .clr(rst));
  Multiplexer #(.width(8), .disabled(0), .enable("false")) multiplexer_3 (
    .in0(reg_i_q), .out(multiplexer_3_out), .sel(selSum0min));  // open: in1
  Multiplexer #(.width(8), .disabled(0), .enable("false")) multiplexer_4 (
    .in0(reg_i_q), .in1(reg_J_q), .out(multiplexer_4_out), .sel(selInc));
  // Probe on nothing
  Register reg_min (.D(multiplexer_3_out), .en(wrMin), .clk(clk), .clr(rst));  // open: Q
  Adder adder_1 (.a(multiplexer_4_out), .b(8'h1), .out(adder_1_out));  // open: cin, cout
  // Probe on multiplexer_5_out
  Multiplexer #(.width(8), .disabled(0), .enable("false")) multiplexer_5 (
    .in0(adder_1_out), .in1(reg_J_q), .out(multiplexer_5_out), .sel(selComp));
  Subtractor subtractor_1 (
    .a(multiplexer_5_out), .b(reg_size_q), .out({lt_size, subtractor_1_out}));  // open: bin, bout

  // Notes on the sheet:
  //   i++
  //   i ^ min
  //   ld address
  //   i++
  //   j++
endmodule
